# Fritzing sketch CANDLE_BRAH_WIRING (saved by Fritzing 0.9.3b)

parts:
  IRF520_MOSFET_Driver_Module = IFR520 MOS module [package=THT]  # not connected
  FLAME_SENSOR = KY-026  # not connected
  SHOULDER_SERVO = Basic Servo  # not connected
  Spark_Gap_400kV_Boost_Step-up_Transformer = Transformer [package=transformer]  # not connected
  5VDC_4A = Power Jack [package=power_jack_combo]
  C1_-_1000uF_16V = Capacitor Polarized [package=cpol-radial-1000uf-25v]  # not connected
  C2_-_1000uF_16V = Capacitor Polarized [package=cpol-radial-1000uf-25v]
  GAS_VALVE_SERVO = Basic Servo  # not connected
  PWR_SWITCH = Taiway 100-SP-X-T1 SPDT Miniature Toggle Switch [part_number=100-SP-X-T1-0-0-B1-M2 package=THT]
  R1 = Resistor [tolerance=±5% resistance=10k package=THT]  # not connected
  U1 = NodeMCU V1.0  # not connected
  ACTIVATE_BUTTON = Arcade Button (red)  # not connected

nets:
  N1: 5VDC_4A.PWR, PWR_SWITCH.COM
  N2: C2_-_1000uF_16V.-, PWR_SWITCH.L1

notes:
  Gas ignition spark gap

custom parts:
  KY-026: ky-026 flame sensor module
  NodeMCU V1.0: ESP8266 based NodeMCU V1.0
  Arcade Button (red): Adafruit Arcade Button (red)
